# Fritzing sketch 基本電路_Bluetooth (saved by Fritzing 0.9.2b)
breadboards: 1

parts:
  Ameba1 = Ameba
  Part2 = Bluetooth HC-05 Macho

nets:
  N1: Ameba1.D0, Part2.TXD
  N2: Ameba1.D1, Part2.RXD
  GND: Ameba1.GND, Part2.GND
  5V: Ameba1.5V, Part2.VCC

custom parts:
  Ameba: Ameba EVB
